// Logisim project 4-1.circ as structural Verilog: 2 circuits, main circuit main
module main (
  input  [7:0] in_1,
  input  [7:0] in_2,
  input  [7:0] in_3
);

  wire main_1_b, main_2_b, main_3_b, main_4_b, main_5_b, main_6_b, main_7_b;
  wire [7:0] main_1_d;

  // Probe on in_3
  // Probe on in_1
  lib_main main_1 (.x1(in_1[0]), .x2(in_3[0]), .x3(1'b0), .d(main_1_d[0]), .b(main_1_b));
  lib_main main_2 (.x1(in_1[1]), .x2(in_3[1]), .x3(main_1_b), .d(main_1_d[1]), .b(main_2_b));
  lib_main main_3 (.x1(in_1[2]), .x2(in_3[2]), .x3(main_2_b), .d(main_1_d[2]), .b(main_3_b));
  lib_main main_4 (.x1(in_1[3]), .x2(in_3[3]), .x3(main_3_b), .d(main_1_d[3]), .b(main_4_b));
  lib_main main_5 (.x1(in_1[4]), .x2(in_3[4]), .x3(main_4_b), .d(main_1_d[4]), .b(main_5_b));
  lib_main main_6 (.x1(in_1[5]), .x2(in_3[5]), .x3(main_5_b), .d(main_1_d[5]), .b(main_6_b));
  lib_main main_7 (.x1(in_1[6]), .x2(in_3[6]), .x3(main_6_b), .d(main_1_d[6]), .b(main_7_b));
  lib_main main_8 (.x1(in_1[7]), .x2(in_3[7]), .x3(main_7_b), .d(main_1_d[7]));  // open: b
  // Probe on main_1_d
endmodule

module lib (
  input  x1,
  input  x2,
  input  x3,
  output d,
  output b
);

  wire and_1_out, and_2_out, and_3_out, and_4_out, and_5_out, and_6_out, and_7_out, not_1_out, not_2_out,
       not_3_out, not_4_out, not_5_out, not_6_out, not_7_out, not_8_out;

  not not_1 (not_1_out, x3);
  not not_2 (not_2_out, x1);
  not not_3 (not_3_out, x2);
  not not_4 (not_4_out, x1);
  not not_5 (not_5_out, x2);
  not not_6 (not_6_out, x3);
  not not_7 (not_7_out, x1);
  not not_8 (not_8_out, x1);
  and and_1 (and_1_out, x2, x3, x1);
  and and_2 (and_2_out, x2, not_1_out, not_2_out);
  and and_3 (and_3_out, not_3_out, x3, not_4_out);
  and and_4 (and_4_out, not_5_out, not_6_out, x1);
  and and_5 (and_5_out, x2, x3);
  and and_6 (and_6_out, x3, not_7_out);
  and and_7 (and_7_out, x2, not_8_out);
  or or_1 (d, and_1_out, and_2_out, and_3_out, and_4_out);
  or or_2 (b, and_5_out, and_6_out, and_7_out);
endmodule
