// Logisim project main.circ as structural Verilog: 5 circuits, main circuit main
module main (
  input  V,
  output out_2,
  output out_3,
  output out_4
);

  wire and_1_out, and_2_out, clock_1_out, not_1_out, not_2_out;

  Clock clock_1 (.out(clock_1_out));
  T_Flip_Flop t_ff_1 (.clk(clock_1_out), .T(V), .Q(out_4));  // open: Qn, preset, reset, en
  not not_1 (not_1_out, out_4);
  T_Flip_Flop t_ff_2 (.clk(clock_1_out), .T(and_1_out), .Q(out_3));  // open: Qn, preset, reset, en
  not not_2 (not_2_out, out_3);
  and and_1 (and_1_out, not_1_out, V);
  T_Flip_Flop t_ff_3 (.clk(clock_1_out), .T(and_2_out), .Q(out_2));  // open: Qn, preset, reset, en
  and and_2 (and_2_out, not_2_out, not_1_out, V);

  // Notes on the sheet:
  //   q1*
  //   q2*
  //   q3*
endmodule

module T_trigger (
  input  in_1,
  output out_2
);

  wire clock_1_out;

  Clock clock_1 (.out(clock_1_out));
  T_Flip_Flop t_ff_1 (.clk(clock_1_out), .T(in_1), .Q(out_2));  // open: Qn, preset, reset, en
endmodule

module D_trigger (
  input  in_1,
  output out_2
);

  wire clock_1_out;

  Clock clock_1 (.out(clock_1_out));
  D_Flip_Flop d_ff_1 (.clk(clock_1_out), .D(in_1), .Q(out_2));  // open: Qn, preset, en, reset
endmodule

module RS_trigger (
  input  in_1,
  input  in_2,
  output out_3
);

  wire clock_1_out;

  Clock clock_1 (.out(clock_1_out));
  S_R_Flip_Flop s_r_ff_1 (.S(in_1), .clk(clock_1_out), .R(in_2), .Q(out_3));  // open: Qn, preset, reset, en
endmodule

module JK_trigger (
  input  in_1,
  input  in_2,
  output out_3
);

  wire clock_1_out;

  Clock clock_1 (.out(clock_1_out));
  J_K_Flip_Flop j_k_ff_1 (.J(in_1), .clk(clock_1_out), .K(in_2), .Q(out_3));  // open: Qn, preset, en, reset
endmodule
